# Fritzing sketch LoRa based smart meter (saved by Fritzing 0.9.3b)
breadboards: 1

parts:
  LoRa_Module1 = Ra-01 - LoRa Module SX1278 [part_number=SX1278]
  U1 = ACS712 [package=so08]
  U2 = Transformer [package=transformer_smd]
  V1 = AC Power [voltage=5 frequency=60]
  R1 = Resistor [tolerance=±5% resistance=220 package="0603 [SMD]"]
  Part2 = Voltage Sensor Module
  JP1 = Header 4 [package=screwterminal-3.5mm-4_lock]
  JP2 = Header 4 [package=screwterminal-3.5mm-4_lock]
  Part3 = Arduino Uno (Rev3)

nets:
  N1: LoRa_Module1.NSS, Part3.D10_PWM/SS
  N2: LoRa_Module1.MOSI, Part3.D11_PWM/MOSI
  N3: LoRa_Module1.MISO, Part3.D12/MISO
  N4: LoRa_Module1.SCK, Part3.D13/SCK
  N5: LoRa_Module1.GND, JP2.4
  3.3V: LoRa_Module1.3.3V, Part3.3V3
  N6: LoRa_Module1.RESET, Part3.D5_PWM
  N7: LoRa_Module1.DIO0, Part3.D2
  N8: LoRa_Module1.DIO1, Part3.D3_PWM
  N9: U1.IP+, V1.V+
  N10: U1.IP-, U2.1
  N11: U1.GND, JP2.2
  N12: U1.VOUT, Part3.A1
  N13: U1.VCC, JP1.3
  N14: U2.2, V1.V-, R1.Pin_1
  N15: U2.3, Part2.INPUT-
  N16: U2.4, Part2.INPUT+
  N17: Part2.GND, JP2.3
  N18: Part2.OUT, Part3.A0
  VCC: Part2.VCC, JP1.4, Part3.5V
  N19: JP2.1, Part3.GND

custom parts:
  Ra-01 - LoRa Module SX1278: The Ra-01 LoRa Module featuring the SX1278 engine by Semtech. Module by AI-Thinker. Module (Ra-01) specifications from: https://www.banggood.com/Ra-01-Smart-Electronics-SX1278-LoRa-Spread-Spectrum-Wireless-Module-Ultra-Far-10KM-433M-p-1130769.html Description: Power supply: DC1.8-3.7V(3.3V) Chip: SX1278 Frequency: 433Mhz Operating temperature: -40~+85°C On Sheild Description (may vary by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
