# Fritzing sketch LoRa gateway with eithernet (saved by Fritzing 0.9.3b)
breadboards: 1

parts:
  LoRa_Module1 = Ra-01 - LoRa Module SX1278 [part_number=SX1278]
  Part3 = Arduino Uno (Rev3)
  Part4 = Arduino Ethernet Shield (Rev3)

nets:
  N1: LoRa_Module1.NSS, Part3.D10_PWM/SS
  N2: LoRa_Module1.MOSI, Part3.D11_PWM/MOSI
  N3: LoRa_Module1.MISO, Part3.D12/MISO
  N4: LoRa_Module1.SCK, Part3.D13/SCK
  GND: LoRa_Module1.GND, Part3.GND, Part4.GND
  3.3V: LoRa_Module1.3.3V, Part3.3V3
  N5: LoRa_Module1.RESET, Part3.D5_PWM
  N6: LoRa_Module1.DIO0, Part3.D2
  N7: LoRa_Module1.DIO1, Part3.D3_PWM
  N8: Part3.A4/SDA, Part4.A4/SDA
  N9: Part3.A5/SCL, Part4.A5/SCL

custom parts:
  Ra-01 - LoRa Module SX1278: The Ra-01 LoRa Module featuring the SX1278 engine by Semtech. Module by AI-Thinker. Module (Ra-01) specifications from: https://www.banggood.com/Ra-01-Smart-Electronics-SX1278-LoRa-Spread-Spectrum-Wireless-Module-Ultra-Far-10KM-433M-p-1130769.html Description: Power supply: DC1.8-3.7V(3.3V) Chip: SX1278 Frequency: 433Mhz Operating temperature: -40~+85°C On Sheild Description (may vary by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
